# Fritzing sketch ldr_setup (saved by Fritzing 0.9.3b)
breadboards: 3

parts:
  Raspberry_Pi_1 = Raspberry Pi 3 [part_number=RPI-3-V1.2]
  IC1 = MCP3008 8-channel 10-bit ADC [part_number=MCP3008]
  P1 = S1133 Si Photodiode [package="8mm Ceramic [THT]"]
  LED1 = RGB LED - (4 legs) [package="5 mm [THT]"]

nets:
  N1: Raspberry_Pi_1.3v3, IC1.no_name_yet#16, P1.anode
  N2: Raspberry_Pi_1.GIPO10, IC1.no_name_yet#11
  N3: Raspberry_Pi_1.GIPO9, IC1.no_name_yet#12
  N4: Raspberry_Pi_1.GIPO11, IC1.no_name_yet#13
  N5: Raspberry_Pi_1.GIPO19, LED1.red_cathode
  N6: Raspberry_Pi_1.GIPO26, LED1.blue_cathode
  N7: Raspberry_Pi_1.GIPO21, LED1.green_cathode
  N8: Raspberry_Pi_1.GIPO8, IC1.no_name_yet#10
  N9: Raspberry_Pi_1.GND, IC1.no_name_yet#9, IC1.no_name_yet#14, IC1.no_name_yet#15, LED1.common_anode
  N10: IC1.no_name_yet#2, P1.cathode

// code stored in the sketch: Untitled.ino
#!/usr/bin/python
import matplotlib.pyplot as plt
from gpiozero import MCP3208
from gpiozero import LED

print('Initialising. Please wait...')

def getdata(mlvol):
  from time import sleep
  import numpy as np

  #initialise plotting parameters
  tint = 0
  tplot = []
  voltarray = []
  plt.ion()

  delay = 0.005

  print("Running program. Please wait...")

  for i in range(1,50):
    adc = MCP3208(channel=1)
    voltage = 3.3*adc.value
    tint += delay
    tplot.append(tint)
    voltarray.append(voltage)

  voltavg = sum(voltarray)/float(len(voltarray))
  #voltavg = np.mean(voltarray)
  #voltsd = np.std(voltarray)
  print("--------------------------------------------")
  print("Mean Voltage: {}V".format(voltavg))
  #print("Standard Deviation: {}V".format(voltsd))

  f = open('data/' + str(mlvol) + 'ml.dat','w+')
  f.write(str(voltavg))
  f.close()

  return voltavg

whitelight = LED(21)
whitelight.on()

lighton = str(input('Is the LED lit? (y/n) '))
if lighton != 'y':
  print('Error. Exiting.')
  quit()
  
runagain = 'y'
voltavg = []
mlvol = []

while runagain == 'y':
  mlvol.append(input('How many ml do you have? '))
  voltavg.append(getdata(mlvol))
  runagain = str(input('Would you like to run another trial? (y/n) '))

whitelight.off()

plt.plot(mlvol,voltavg,'ko',markerfacecolor = 'r')
plt.plot(mlvol,voltavg,'b',linewidth = 1.5)
plt.xlabel('ml')
plt.ylabel('V')
plt.ylim(0,3.3)
