# Fritzing sketch tmp_setup (saved by Fritzing 0.9.3b)
breadboards: 1

parts:
  Raspberry_Pi_1 = Raspberry Pi 3 [part_number=RPI-3-V1.2]
  IC1 = MCP3008 8-channel 10-bit ADC [part_number=MCP3008]
  LED1 = LED - 5mm [color="Red (633nm)" package="5 mm [THT]"]
  T1 = LM35 Temperature Sensor [package="TO92 [THT]"]

nets:
  N1: Raspberry_Pi_1.3v3, IC1.no_name_yet#15, IC1.no_name_yet#16, T1.+Vs
  N2: Raspberry_Pi_1.GIPO17, LED1.anode
  N3: Raspberry_Pi_1.GIPO10, IC1.no_name_yet#11
  N4: Raspberry_Pi_1.GIPO9, IC1.no_name_yet#12
  N5: Raspberry_Pi_1.GIPO11, IC1.no_name_yet#13
  GND: Raspberry_Pi_1.GND, IC1.no_name_yet#9, IC1.no_name_yet#14, LED1.cathode, T1.GND
  N6: Raspberry_Pi_1.GIPO8, IC1.no_name_yet#10
  N7: IC1.no_name_yet#8, T1.Vout

// code stored in the sketch: Untitled.ino
from gpiozero import MCP3208, LED
from time import sleep
import matplotlib.pyplot as plt

#initialise LED
red_led = LED(17)

#initialise plotting parameters
tint = 0
tplot = []
lplot = []
plt.ion()

delay = 0.05

while True:
	tmp = MCP3208(channel=0)
	temperature = (tmp.value*3.3-0.5)*100

	if (temperature >= 25):
		red_led.on()
	else:
		red_led.off()

	#print results
	print("------------------------------")
	print("Temp: {}C".format(temperature))

	tint += delay
	tplot.append(tint)

	lplot.append(voltage)

	plt.plot(tplot,lplot)
	plt.ylim(0,35)
	plt.show()
	plt.pause(delay)
